// Logisim project add_sub_circuit.circ as structural Verilog: 1 circuit, main circuit main
module main (
  input  ADD,
  input  SUB,
  input  B0,
  input  B1,
  input  B2,
  input  B3
);

  wire adder_1_cout, adder_1_out, adder_2_cout, adder_2_out, adder_3_cout, adder_3_out, adder_4_cout,
       adder_4_out, and_1_out, and_2_out, and_3_out, and_4_out, and_5_out, and_6_out, and_7_out, and_8_out,
       clock_1_out, clock_2_out, d_ff_1_q, d_ff_1_qn, d_ff_2_q, d_ff_2_qn, d_ff_3_q, d_ff_3_qn, d_ff_4_q,
       d_ff_4_qn, d_ff_5_q, d_ff_6_q, d_ff_7_q, d_ff_8_q, or_1_out, or_2_out, or_3_out, or_4_out;

  Clock clock_1 (.out(clock_1_out));
  D_Flip_Flop d_ff_1 (.clk(clock_1_out), .D(B0), .Q(d_ff_1_q), .Qn(d_ff_1_qn), .en(1'b1));  // open: preset, reset
  D_Flip_Flop d_ff_2 (.clk(clock_1_out), .D(B1), .Q(d_ff_2_q), .Qn(d_ff_2_qn), .en(1'b1));  // open: preset, reset
  D_Flip_Flop d_ff_3 (.clk(clock_1_out), .D(B2), .Q(d_ff_3_q), .Qn(d_ff_3_qn), .en(1'b1));  // open: preset, reset
  D_Flip_Flop d_ff_4 (.clk(clock_1_out), .D(B3), .Q(d_ff_4_q), .Qn(d_ff_4_qn), .en(1'b1));  // open: preset, reset
  and and_1 (and_1_out, d_ff_1_q, ADD);
  and and_2 (and_2_out, d_ff_2_q, ADD);
  and and_3 (and_3_out, d_ff_3_q, ADD);
  and and_4 (and_4_out, d_ff_4_q, ADD);
  and and_5 (and_5_out, d_ff_1_qn, SUB);
  and and_6 (and_6_out, d_ff_2_qn, SUB);
  and and_7 (and_7_out, d_ff_3_qn, SUB);
  and and_8 (and_8_out, d_ff_4_qn, SUB);
  or or_1 (or_1_out, and_1_out, and_5_out);
  or or_2 (or_2_out, and_2_out, and_6_out);
  or or_3 (or_3_out, and_3_out, and_7_out);
  or or_4 (or_4_out, and_4_out, and_8_out);
  LED C4 (.in(adder_4_cout));
  Adder #(.width(1)) adder_1 (.a(or_1_out), .b(d_ff_5_q), .out(adder_1_out), .cin(SUB), .cout(adder_1_cout));
  Adder #(.width(1)) adder_2 (.a(or_2_out), .b(d_ff_6_q), .out(adder_2_out), .cin(adder_1_cout), .cout(adder_2_cout));
  Adder #(.width(1)) adder_3 (.a(or_3_out), .b(d_ff_7_q), .out(adder_3_out), .cin(adder_2_cout), .cout(adder_3_cout));
  Adder #(.width(1)) adder_4 (.a(or_4_out), .b(d_ff_8_q), .out(adder_4_out), .cin(adder_3_cout), .cout(adder_4_cout));
  Clock clock_2 (.out(clock_2_out));
  D_Flip_Flop d_ff_5 (.clk(clock_2_out), .D(adder_1_out), .Q(d_ff_5_q), .en(1'b1));  // open: Qn, preset, reset
  D_Flip_Flop d_ff_6 (.clk(clock_2_out), .D(adder_2_out), .Q(d_ff_6_q), .en(1'b1));  // open: Qn, preset, reset
  D_Flip_Flop d_ff_7 (.clk(clock_2_out), .D(adder_3_out), .Q(d_ff_7_q), .en(1'b1));  // open: Qn, preset, reset
  D_Flip_Flop d_ff_8 (.clk(clock_2_out), .D(adder_4_out), .Q(d_ff_8_q), .en(1'b1));  // open: Qn, preset, reset
  LED A0 (.in(d_ff_5_q));
  LED A1 (.in(d_ff_6_q));
  LED A2 (.in(d_ff_7_q));
  LED A3 (.in(d_ff_8_q));

  // Notes on the sheet:
  //   C0
endmodule
