// Logisim project equality_checker.circ as structural Verilog: 1 circuit, main circuit main
module main (
  input  in_1,
  input  in_2,
  input  in_3,
  input  in_4
);

  wire and_1_out, xnor_1_out, xnor_2_out;

  xnor xnor_1 (xnor_1_out, in_1, in_3);
  xnor xnor_2 (xnor_2_out, in_2, in_4);
  and and_1 (and_1_out, xnor_1_out, xnor_2_out);
  LED led_1 (.in(and_1_out));
endmodule
