// Logisim project even_parity_generator.circ as structural Verilog: 1 circuit, main circuit main
module main (
  input  D3,
  input  D2,
  input  D1,
  input  D0
);

  wire xor_1_out, xor_2_out, xor_3_out;

  xor xor_1 (xor_1_out, D3, D2);
  xor xor_2 (xor_2_out, D1, D0);
  LED P (.in(xor_3_out));
  xor xor_3 (xor_3_out, xor_1_out, xor_2_out);
  LED led_1 (.in(D0));
  LED led_2 (.in(D1));
  LED led_3 (.in(D2));
  LED led_4 (.in(D3));
endmodule
