// Logisim project latch_d.circ as structural Verilog: 1 circuit, main circuit main
module main (
  input  D,
  input  E
);

  wire and_1_out, and_2_out, nor_1_out, nor_2_out, not_1_out;

  not not_1 (not_1_out, D);
  and and_1 (and_1_out, D, E);
  and and_2 (and_2_out, E, not_1_out);
  nor nor_1 (nor_1_out, and_1_out, nor_2_out);
  nor nor_2 (nor_2_out, nor_1_out, and_2_out);
  LED Q_prime (.in(nor_1_out));
  LED Q (.in(nor_2_out));
endmodule
