// Logisim project latch_sr_enable.circ as structural Verilog: 1 circuit, main circuit main
module main (
  input  S,
  input  E,
  input  R
);

  wire and_1_out, and_2_out, nor_1_out, nor_2_out;

  and and_1 (and_1_out, S, E);
  and and_2 (and_2_out, E, R);
  nor nor_1 (nor_1_out, and_1_out, nor_2_out);
  nor nor_2 (nor_2_out, nor_1_out, and_2_out);
  LED Q_prime (.in(nor_1_out));
  LED Q (.in(nor_2_out));
endmodule
